# Fritzing sketch chickenhouse (saved by Fritzing 0.9.2b)
breadboards: 1

parts:
  Bauteil1 = Arduino Uno (Rev3)
  Bauteil2 = Arduino Ethernet Shield (Rev3)
  DHT1 = DHT22 Humidity and Temperature Sensor
  S2 = Pushbutton [package="[THT]"]

nets:
  N1: Bauteil1.A5/SCL, DHT1.DATA
  N2: Bauteil1.D10_PWM/SS, Bauteil2.ETH_CS
  N3: Bauteil1.D11_PWM/MOSI, Bauteil2.PWM_D11
  N4: Bauteil1.D12/MISO, Bauteil2.SPI/D12
  N5: Bauteil1.D13/SCK, Bauteil2.SPI/D13
  5V: Bauteil1.5V, DHT1.VDD
  GND: Bauteil1.GND, DHT1.GND
  N6: S2.Pin_1, S2.Pin_2
  N7: S2.Pin_3, S2.Pin_4
